# Fritzing sketch liikennevalot (saved by Fritzing 0.9.3b)
breadboards: 1

parts:
  Part2 = Adafruit T-Cobbler Plus [part_number="Adafruit #1989 and #2028"]
  S1 = Pushbutton [package="[THT]"]
  LED1 = LED - 5mm [color="Red (633nm)" package="5 mm [THT]"]
  LED2 = LED - 5mm [color="Red (633nm)" package="5 mm [THT]"]
  LED3 = LED - 5mm [color="Red (633nm)" package="5 mm [THT]"]
  R1 = Resistor [tolerance=±0.05% resistance=10 package=THT]
  R2 = Resistor [tolerance=±1% resistance=10 package=THT]
  R3 = Resistor [tolerance=±1% resistance=10 package=THT]
  R4 = Resistor [tolerance=±1% resistance=10 package=THT]
  LED4 = LED - 5mm [color="Red (633nm)" package="5 mm [THT]"]
  LED5 = LED - 5mm [color="Red (633nm)" package="5 mm [THT]"]
  LED6 = LED - 5mm [color="Red (633nm)" package="5 mm [THT]"]
  R5 = Resistor [tolerance=±5% resistance=220 package=THT]
  R6 = Resistor [tolerance=±5% resistance=220 package=THT]
  R7 = Resistor [tolerance=±5% resistance=220 package=THT]
  PIR1 = PIR sensor

nets:
  N1: Part2.+3.3V_2, S1.Pin_3, S1.Pin_4
  +5V: Part2.+5V, PIR1.VDD
  GND: Part2.GND, R5.Pin_1, R6.Pin_1, R7.Pin_1, PIR1.GND
  N2: Part2.GPIO25, PIR1.SIG
  N3: Part2.GPIO16, LED6.anode
  N4: Part2.GPIO20, LED5.anode
  N5: Part2.GPIO21, LED4.anode
  N6: S1.Pin_1, S1.Pin_2, R1.Pin_1
  N7: LED1.cathode, R2.Pin_1
  N8: LED2.cathode, R3.Pin_1
  N9: LED3.cathode, R4.Pin_1
  N10: R1.Pin_0, R2.Pin_0, R3.Pin_0, R4.Pin_0
  N11: LED4.cathode, R7.Pin_0
  N12: LED5.cathode, R5.Pin_0
  N13: LED6.cathode, R6.Pin_0

custom parts:
  Adafruit T-Cobbler Plus: The Raspberry Pi has landed on the Maker World like a 40-GPIO pinned, quad-USB ported, credit card sized bomb of DIY joy. And while you can use most of our great Model B accessories by hooking up our downgrade cable, its probably a good time to upgrade your set up and accessorize using all of the 40 pins. That's why we now carry the Assembled Adafruit Pi T-Cobbler Plus - Breakout + Cable for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
